// Logisim project physical.circ as structural Verilog: 2 circuits, main circuit main
module main (
);

  wire undriven, undriven_2, undriven_3, undriven_4, undriven_6, undriven_7, undriven_8, undriven_9;
  wire [3:0] undriven_5;
  wire [63:0] A_q, alu_1_outp, alu_2_outp, alu_3_outp, alu_4_outp, B_q, C_q, controlled_buffer_1_out, D_q;

  Counter #(.max('hffffffffffffffff), .width(64)) counter_1 ();  // open: load, D, count, Q, carry, up, clk, clr
  Register #(.width(64)) A (.D(controlled_buffer_1_out), .Q(A_q));  // open: en, clk, clr
  Register #(.width(64)) B (.D(controlled_buffer_1_out), .Q(B_q));  // open: en, clk, clr
  Register #(.width(64)) C (.D(controlled_buffer_1_out), .Q(C_q));  // open: en, clk, clr
  Register #(.width(64)) D (.D(controlled_buffer_1_out), .Q(D_q));  // open: en, clk, clr
  assign controlled_buffer_1_out = undriven ? A_q : 64'bz;  // Controlled_Buffer controlled_buffer_1
  assign controlled_buffer_1_out = undriven_2 ? B_q : 64'bz;  // Controlled_Buffer controlled_buffer_2
  assign controlled_buffer_1_out = undriven_3 ? C_q : 64'bz;  // Controlled_Buffer controlled_buffer_3
  assign controlled_buffer_1_out = undriven_4 ? D_q : 64'bz;  // Controlled_Buffer controlled_buffer_4
  alu alu_1 (.InA(A_q), .InB(B_q), .Control(undriven_5), .outp(alu_1_outp));  // open: gt, eq, lt
  alu alu_2 (.InA(C_q), .InB(D_q), .Control(undriven_5), .outp(alu_2_outp));  // open: gt, eq, lt
  alu alu_3 (.InA(A_q), .InB(C_q), .Control(undriven_5), .outp(alu_3_outp));  // open: gt, eq, lt
  alu alu_4 (.InA(B_q), .InB(D_q), .Control(undriven_5), .outp(alu_4_outp));  // open: gt, eq, lt
  assign controlled_buffer_1_out = undriven_6 ? alu_1_outp : 64'bz;  // Controlled_Buffer ACCA
  assign controlled_buffer_1_out = undriven_7 ? alu_2_outp : 64'bz;  // Controlled_Buffer ACCB
  assign controlled_buffer_1_out = undriven_8 ? alu_3_outp : 64'bz;  // Controlled_Buffer ACCC
  assign controlled_buffer_1_out = undriven_9 ? alu_4_outp : 64'bz;  // Controlled_Buffer ACCD
endmodule

module alu (
  input  [63:0] InA,
  input  [63:0] InB,
  input  [3:0] Control,
  output gt,
  output eq,
  output lt,
  output [63:0] outp
);

  wire [63:0] adder_1_out, and_1_out, multiplier_1_out, not_1_out, or_1_out, shifter_1_out, shifter_2_out,
       subtractor_1_out, undriven, undriven_2, xor_1_out;

  Comparator #(.mode("unsigned"), .width(64)) comparator_1 (.a(InA), .b(InB), .gt(gt), .eq(eq), .lt(lt));
  Adder #(.width(64)) adder_1 (.a(InA), .b(InB), .out(adder_1_out));  // open: cin, cout
  Subtractor #(.width(64)) subtractor_1 (.a(InA), .b(InB), .out(subtractor_1_out));  // open: bin, bout
  Multiplier #(.width(64)) multiplier_1 (.a(InA), .b(InB), .out(multiplier_1_out));  // open: cin, cout
  Shifter #(.shift("rl"), .width(64)) shifter_1 (.in(InA), .\dist (InB[5:0]), .out(shifter_1_out));
  Shifter #(.shift("rr"), .width(64)) shifter_2 (.in(InA), .\dist (InB[5:0]), .out(shifter_2_out));
  assign or_1_out = InA | InB;  // OR_Gate or_1, 64 bits wide
  assign not_1_out = ~InA;  // NOT_Gate not_1, 64 bits wide
  assign xor_1_out = InA ^ InB;  // XOR_Gate xor_1, 64 bits wide
  assign and_1_out = InA & InB;  // AND_Gate and_1, 64 bits wide
  Multiplexer #(.disabled("Z"), .select(4), .width(64)) multiplexer_1 (
    .in0(adder_1_out), .in1(subtractor_1_out), .in2(multiplier_1_out), .in3(undriven_2), .in4(undriven),
    .in5(or_1_out), .in6(not_1_out), .in7(xor_1_out), .in8(and_1_out), .in9(shifter_1_out),
    .in10(shifter_2_out), .out(outp), .sel(Control));  // open: in11, in12, in13, in14, in15
endmodule
